// Digital circuit 2-bit-multiplier.dig as structural Verilog
module _2_bit_multiplier (
  input  [1:0] A,
  input  [1:0] B,
  output [3:0] Output
);

  wire and_3_out, and_4_out, and_5_out;

  and and_1 (Output[0], A[0], B[0]);
  and and_2 (Output[0], A[0], B[1]);
  and and_3 (and_3_out, A[1], B[0]);
  and and_4 (and_4_out, A[1], B[1]);
  xor xor_1 (Output[1], Output[0], and_3_out);
  and and_5 (and_5_out, Output[0], Output[0]);
  xor xor_2 (Output[2], and_5_out, and_4_out);
  and and_6 (Output[3], and_4_out, Output[0]);
endmodule
