// Digital circuit 4-bit-DRAM.dig as structural Verilog
module _4_bit_DRAM (
  input  clock,
  input  [3:0] Address,
  input  [3:0] \input ,
  input  [1:0] ctrl,
  output [3:0] \output 
);

  wire and_1_out, and_2_out, and_3_out, and_4_out, and_5_out, and_6_out, and_7_out, and_8_out, and_9_out,
       and_10_out, and_11_out, and_12_out, and_13_out, and_14_out, and_15_out, and_16_out, decoder_1_out_0,
       decoder_1_out_1, decoder_1_out_2, decoder_1_out_3, decoder_1_out_4, decoder_1_out_5, decoder_1_out_6,
       decoder_1_out_7, decoder_1_out_8, decoder_1_out_9, decoder_1_out_10, decoder_1_out_11,
       decoder_1_out_12, decoder_1_out_13, decoder_1_out_14, decoder_1_out_15;
  wire [3:0] _4_bit_register_1_output, _4_bit_register_2_output, _4_bit_register_3_output,
       _4_bit_register_4_output, _4_bit_register_5_output, _4_bit_register_6_output,
       _4_bit_register_7_output, _4_bit_register_8_output, _4_bit_register_9_output,
       _4_bit_register_10_output, _4_bit_register_11_output, _4_bit_register_12_output,
       _4_bit_register_13_output, _4_bit_register_14_output, _4_bit_register_15_output,
       _4_bit_register_16_output;

  Decoder #(.Selector_Bits(4)) decoder_1 (
    .sel(Address), .out_0(decoder_1_out_0), .out_1(decoder_1_out_1), .out_2(decoder_1_out_2),
    .out_3(decoder_1_out_3), .out_4(decoder_1_out_4), .out_5(decoder_1_out_5), .out_6(decoder_1_out_6),
    .out_7(decoder_1_out_7), .out_8(decoder_1_out_8), .out_9(decoder_1_out_9), .out_10(decoder_1_out_10),
    .out_11(decoder_1_out_11), .out_12(decoder_1_out_12), .out_13(decoder_1_out_13),
    .out_14(decoder_1_out_14), .out_15(decoder_1_out_15));
  and and_1 (and_1_out, clock, decoder_1_out_0);
  and and_2 (and_2_out, clock, decoder_1_out_1);
  and and_3 (and_3_out, clock, decoder_1_out_2);
  and and_4 (and_4_out, clock, decoder_1_out_3);
  and and_5 (and_5_out, clock, decoder_1_out_4);
  and and_6 (and_6_out, clock, decoder_1_out_5);
  and and_7 (and_7_out, clock, decoder_1_out_6);
  and and_8 (and_8_out, clock, decoder_1_out_7);
  and and_9 (and_9_out, clock, decoder_1_out_8);
  and and_10 (and_10_out, clock, decoder_1_out_9);
  and and_11 (and_11_out, clock, decoder_1_out_10);
  and and_12 (and_12_out, clock, decoder_1_out_11);
  and and_13 (and_13_out, clock, decoder_1_out_12);
  and and_14 (and_14_out, clock, decoder_1_out_13);
  and and_15 (and_15_out, clock, decoder_1_out_14);
  and and_16 (and_16_out, clock, decoder_1_out_15);
  _4_bit_register _4_bit_register_1 (
    .clock(and_1_out), .\input (\input ), .ctrl(ctrl), .\output (_4_bit_register_1_output));
  _4_bit_register _4_bit_register_2 (
    .clock(and_2_out), .\input (\input ), .ctrl(ctrl), .\output (_4_bit_register_2_output));
  _4_bit_register _4_bit_register_3 (
    .clock(and_3_out), .\input (\input ), .ctrl(ctrl), .\output (_4_bit_register_3_output));
  _4_bit_register _4_bit_register_4 (
    .clock(and_4_out), .\input (\input ), .ctrl(ctrl), .\output (_4_bit_register_4_output));
  _4_bit_register _4_bit_register_5 (
    .clock(and_5_out), .\input (\input ), .ctrl(ctrl), .\output (_4_bit_register_5_output));
  _4_bit_register _4_bit_register_6 (
    .clock(and_6_out), .\input (\input ), .ctrl(ctrl), .\output (_4_bit_register_6_output));
  _4_bit_register _4_bit_register_7 (
    .clock(and_7_out), .\input (\input ), .ctrl(ctrl), .\output (_4_bit_register_7_output));
  _4_bit_register _4_bit_register_8 (
    .clock(and_8_out), .\input (\input ), .ctrl(ctrl), .\output (_4_bit_register_8_output));
  _4_bit_register _4_bit_register_9 (
    .clock(and_9_out), .\input (\input ), .ctrl(ctrl), .\output (_4_bit_register_9_output));
  _4_bit_register _4_bit_register_10 (
    .clock(and_10_out), .\input (\input ), .ctrl(ctrl), .\output (_4_bit_register_10_output));
  _4_bit_register _4_bit_register_11 (
    .clock(and_11_out), .\input (\input ), .ctrl(ctrl), .\output (_4_bit_register_11_output));
  _4_bit_register _4_bit_register_12 (
    .clock(and_12_out), .\input (\input ), .ctrl(ctrl), .\output (_4_bit_register_12_output));
  _4_bit_register _4_bit_register_13 (
    .clock(and_13_out), .\input (\input ), .ctrl(ctrl), .\output (_4_bit_register_13_output));
  _4_bit_register _4_bit_register_14 (
    .clock(and_14_out), .\input (\input ), .ctrl(ctrl), .\output (_4_bit_register_14_output));
  _4_bit_register _4_bit_register_15 (
    .clock(and_15_out), .\input (\input ), .ctrl(ctrl), .\output (_4_bit_register_15_output));
  _4_bit_register _4_bit_register_16 (
    .clock(and_16_out), .\input (\input ), .ctrl(ctrl), .\output (_4_bit_register_16_output));
  Multiplexer #(.Selector_Bits(4), .Bits(4)) multiplexer_1 (
    .sel(Address), .in_0(_4_bit_register_1_output), .in_1(_4_bit_register_2_output),
    .in_2(_4_bit_register_3_output), .in_3(_4_bit_register_4_output), .in_4(_4_bit_register_5_output),
    .in_5(_4_bit_register_6_output), .in_6(_4_bit_register_7_output), .in_7(_4_bit_register_8_output),
    .in_8(_4_bit_register_9_output), .in_9(_4_bit_register_10_output), .in_10(_4_bit_register_11_output),
    .in_11(_4_bit_register_12_output), .in_12(_4_bit_register_13_output), .in_13(_4_bit_register_14_output),
    .in_14(_4_bit_register_15_output), .in_15(_4_bit_register_16_output), .out(\output ));

  // Notes on the sheet:
  //   ctrl: 00 - load
  //   01 - write
  //   10 - clear
endmodule
