// Digital circuit 4-bit-general-purpose-registers.dig as structural Verilog
module _4_bit_general_purpose_registers (
  input  [1:0] ctrl,
  input  [3:0] \input ,
  input  [1:0] Address,
  input  Clock,
  output [3:0] \output 
);

  wire and_1_out, and_2_out, and_3_out, and_4_out, decoder_1_out_0, decoder_1_out_1, decoder_1_out_2,
       decoder_1_out_3;
  wire [3:0] _4_bit_register_1_output, _4_bit_register_2_output, _4_bit_register_3_output,
       _4_bit_register_4_output;

  Decoder #(.Selector_Bits(2)) decoder_1 (
    .sel(Address), .out_0(decoder_1_out_0), .out_1(decoder_1_out_1), .out_2(decoder_1_out_2),
    .out_3(decoder_1_out_3));
  and and_1 (and_1_out, decoder_1_out_3, Clock);
  _4_bit_register _4_bit_register_1 (
    .clock(and_1_out), .\input (\input ), .ctrl(ctrl), .\output (_4_bit_register_1_output));
  and and_2 (and_2_out, decoder_1_out_2, Clock);
  _4_bit_register _4_bit_register_2 (
    .clock(and_2_out), .\input (\input ), .ctrl(ctrl), .\output (_4_bit_register_2_output));
  and and_3 (and_3_out, decoder_1_out_1, Clock);
  _4_bit_register _4_bit_register_3 (
    .clock(and_3_out), .\input (\input ), .ctrl(ctrl), .\output (_4_bit_register_3_output));
  and and_4 (and_4_out, decoder_1_out_0, Clock);
  _4_bit_register _4_bit_register_4 (
    .clock(and_4_out), .\input (\input ), .ctrl(ctrl), .\output (_4_bit_register_4_output));
  Multiplexer #(.Bits(4), .Selector_Bits(2)) multiplexer_1 (
    .sel(Address), .in_0(_4_bit_register_4_output), .in_1(_4_bit_register_3_output),
    .in_2(_4_bit_register_2_output), .in_3(_4_bit_register_1_output), .out(\output ));

  // Notes on the sheet:
  //   ctrl: 00 - load
  //   01 - write
  //   02 - clear
endmodule
