// Digital circuit Registers_DRAM.dig as structural Verilog
module Registers_DRAM (
  input  [1:0] ctrl,
  input  [1:0] ctrl_2,
  input  clock,
  input  in_4,
  input  [3:0] \input ,
  input  [3:0] input_2,
  input  [1:0] ctrl_3,
  input  [1:0] address,
  input  [1:0] ctrl_4,
  input  in_11,
  output [3:0] \output 
);

  wire [3:0] _4_bit_dram_1_output, _4_bit_general_purpose_registers_1_output,
       _4_bit_program_counter_1_output, multiplexer_1_out, multiplexer_2_out;

  _4_bit_DRAM _4_bit_dram_1 (
    .clock(clock), .Address(_4_bit_program_counter_1_output), .\input (input_2), .ctrl(ctrl_3),
    .\output (_4_bit_dram_1_output));
  Multiplexer #(.Bits(4)) multiplexer_1 (
    .sel(in_4), .in_0(_4_bit_general_purpose_registers_1_output), .in_1(_4_bit_dram_1_output),
    .out(multiplexer_1_out));
  _4_bit_program_counter _4_bit_program_counter_1 (
    .ctrl(ctrl_2), .clock(clock), .\output (_4_bit_program_counter_1_output));
  Multiplexer #(.Bits(4)) multiplexer_2 (
    .in_0(\input ), .in_1(_4_bit_dram_1_output), .out(multiplexer_2_out));  // open: sel
  _4_bit_register _4_bit_register_1 (.clock(clock), .\input (multiplexer_1_out), .ctrl(ctrl), .\output (\output ));
  _4_bit_general_purpose_registers _4_bit_general_purpose_registers_1 (
    .ctrl(ctrl_4), .\input (multiplexer_2_out), .Address(address), .Clock(clock),
    .\output (_4_bit_general_purpose_registers_1_output));

  // Notes on the sheet:
  //   ctrl: 00 - load
  //   01 - write
  //   02 - clear
  //   ctrl_2: 00 - load
  //   01 - write
  //   02 - clear
  //   ctrl_3: 00 - load
  //   01 - write
  //   02 - clear
  //   ctrl_4: 00 - load
  //   01 - write
  //   02 - clear
endmodule
