// Digital circuit 4-bit-adder-subtractor.dig as structural Verilog
module _4_bit_adder_subtractor (
  input  [3:0] A,
  input  [3:0] B,
  input  Add_Sub,
  output [3:0] Sum,
  output Overflow
);

  wire _1_bit_adder_2_carry_out, _1_bit_adder_3_carry_out, _1_bit_adder_4_carry_out, not_1_out, xor_1_out,
       xor_2_out, xor_3_out, xor_4_out;

  xor xor_1 (xor_1_out, B[0], Add_Sub);
  xor xor_2 (xor_2_out, B[1], Add_Sub);
  xor xor_3 (xor_3_out, B[2], Add_Sub);
  xor xor_4 (xor_4_out, B[3], Add_Sub);
  _1_bit_adder _1_bit_adder_1 (
    .A(A[3]), .B(xor_4_out), .Carry_in(_1_bit_adder_2_carry_out), .Sum(Sum[3]), .Carry_out(Overflow));
  _1_bit_adder _1_bit_adder_2 (
    .A(A[2]), .B(xor_3_out), .Carry_in(_1_bit_adder_3_carry_out), .Sum(Sum[2]),
    .Carry_out(_1_bit_adder_2_carry_out));
  not not_1 (not_1_out, Add_Sub);
  _1_bit_adder _1_bit_adder_3 (
    .A(A[1]), .B(xor_2_out), .Carry_in(_1_bit_adder_4_carry_out), .Sum(Sum[1]),
    .Carry_out(_1_bit_adder_3_carry_out));
  _1_bit_adder _1_bit_adder_4 (
    .A(A[0]), .B(xor_1_out), .Carry_in(not_1_out), .Sum(Sum[0]), .Carry_out(_1_bit_adder_4_carry_out));
endmodule
