// Digital circuit 4-bit-counter-modified.dig as structural Verilog
module _4_bit_counter_modified (
  input  [1:0] ctrl,
  input  clock,
  input  [3:0] increment,
  output [3:0] \output 
);

  wire [3:0] _4_bit_adder_1_sum, multiplexer_1_out, not_1_out;

  _4_bit_adder _4_bit_adder_1 (.A(\output ), .B(increment), .Sum(_4_bit_adder_1_sum));  // open: Overflow
  assign not_1_out = ~4'b0000;  // Not not_1, 4 bits wide
  Multiplexer #(.Selector_Bits(2), .Bits(4)) multiplexer_1 (
    .sel(ctrl), .in_0(\output ), .in_1(_4_bit_adder_1_sum), .in_2(4'b0000), .in_3(not_1_out),
    .out(multiplexer_1_out));
  D_FF d_ff_1 (.D(multiplexer_1_out[3]), .C(clock), .Q(\output [3]));  // open: nQ
  D_FF d_ff_2 (.D(multiplexer_1_out[2]), .C(clock), .Q(\output [2]));  // open: nQ
  D_FF d_ff_3 (.D(multiplexer_1_out[1]), .C(clock), .Q(\output [1]));  // open: nQ
  D_FF d_ff_4 (.D(multiplexer_1_out[0]), .C(clock), .Q(\output [0]));  // open: nQ
endmodule
