// Digital circuit Register_File_Write_ctrl.dig as structural Verilog
module Register_File_Write_ctrl (
  input  [1:0] Opcode_3,
  output [7:0] write_ctrl
);

  Decoder #(.Selector_Bits(2)) decoder_1 (
    .sel(Opcode_3), .out_0(write_ctrl[0]), .out_1(write_ctrl[2]), .out_2(write_ctrl[4]), .out_3(write_ctrl[6]));

  assign {write_ctrl[7], write_ctrl[5], write_ctrl[3], write_ctrl[1]} = 4'b0000;
endmodule
