// Digital circuit intr-memory-module-16-bit-modified.dig as structural Verilog
module intr_memory_module_16_bit_modified (
  input  clk,
  input  [1:0] ctrl_IR,
  input  [1:0] ctrl_InstruMEM,
  input  [3:0] input_InstruMEM,
  input  [1:0] ctrl_PC,
  output [15:0] output_IR,
  output [3:0] output_pc,
  output [1:0] Enable_alu
);

  wire [1:0] demultiplexer_2_out_0, demultiplexer_2_out_1, demultiplexer_2_out_2, demultiplexer_2_out_3;
  wire [3:0] _4_bit_dram_1_output, demultiplexer_1_out_0, demultiplexer_1_out_1, demultiplexer_1_out_2,
       demultiplexer_1_out_3;

  _4_bit_counter_modified _4_bit_counter_modified_1 (
    .ctrl(ctrl_PC), .clock(clk), .increment(4'b0001), .\output ({output_pc[3:1], Enable_alu[0]}));
  _4_bit_DRAM _4_bit_dram_1 (
    .clock(clk), .Address({output_pc[3:1], Enable_alu[0]}), .\input (input_InstruMEM), .ctrl(ctrl_InstruMEM),
    .\output (_4_bit_dram_1_output));
  Demultiplexer #(.Selector_Bits(2), .Bits(4)) demultiplexer_1 (
    .sel({output_pc[1], Enable_alu[0]}), .in(_4_bit_dram_1_output), .out_0(demultiplexer_1_out_0),
    .out_1(demultiplexer_1_out_1), .out_2(demultiplexer_1_out_2), .out_3(demultiplexer_1_out_3));
  Demultiplexer #(.Selector_Bits(2), .Bits(2)) demultiplexer_2 (
    .sel({output_pc[1], Enable_alu[0]}), .in(ctrl_IR), .out_0(demultiplexer_2_out_0),
    .out_1(demultiplexer_2_out_1), .out_2(demultiplexer_2_out_2), .out_3(demultiplexer_2_out_3));
  _4_bit_register _4_bit_register_1 (
    .clock(clk), .\input (demultiplexer_1_out_0), .ctrl(demultiplexer_2_out_0), .\output (output_IR[3:0]));
  _4_bit_register _4_bit_register_2 (
    .clock(clk), .\input (demultiplexer_1_out_1), .ctrl(demultiplexer_2_out_1), .\output (output_IR[7:4]));
  _4_bit_register _4_bit_register_3 (
    .clock(clk), .\input (demultiplexer_1_out_2), .ctrl(demultiplexer_2_out_2), .\output (output_IR[11:8]));
  _4_bit_register _4_bit_register_4 (
    .clock(clk), .\input (demultiplexer_1_out_3), .ctrl(demultiplexer_2_out_3), .\output (output_IR[15:12]));
  // Pins of 1 and 2 bits meet at Enable_alu

  assign output_pc[0] = Enable_alu[0];

  // Notes on the sheet:
  //   ctrl_PC: default 1
endmodule
