// Digital circuit register-files.dig as structural Verilog
module register_files (
  input  [7:0] ctrl,
  input  [1:0] read_1,
  input  [1:0] read_2,
  input  [3:0] write,
  input  [1:0] select,
  input  clock,
  output [3:0] output_1,
  output [3:0] output_2
);

  wire [3:0] _4_bit_register_1_output, _4_bit_register_2_output, _4_bit_register_3_output,
       _4_bit_register_4_output, demultiplexer_1_out_0, demultiplexer_1_out_1, demultiplexer_1_out_2,
       demultiplexer_1_out_3;

  Demultiplexer #(.Selector_Bits(2), .Bits(4)) demultiplexer_1 (
    .sel(select), .in(write), .out_0(demultiplexer_1_out_0), .out_1(demultiplexer_1_out_1),
    .out_2(demultiplexer_1_out_2), .out_3(demultiplexer_1_out_3));
  _4_bit_register _4_bit_register_1 (
    .clock(clock), .\input (demultiplexer_1_out_0), .ctrl(ctrl[1:0]), .\output (_4_bit_register_1_output));
  _4_bit_register _4_bit_register_2 (
    .clock(clock), .\input (demultiplexer_1_out_1), .ctrl(ctrl[3:2]), .\output (_4_bit_register_2_output));
  _4_bit_register _4_bit_register_3 (
    .clock(clock), .\input (demultiplexer_1_out_2), .ctrl(ctrl[5:4]), .\output (_4_bit_register_3_output));
  _4_bit_register _4_bit_register_4 (
    .clock(clock), .\input (demultiplexer_1_out_3), .ctrl(ctrl[7:6]), .\output (_4_bit_register_4_output));
  Multiplexer #(.Selector_Bits(2), .Bits(4)) multiplexer_1 (
    .sel(read_1), .in_0(_4_bit_register_1_output), .in_1(_4_bit_register_2_output),
    .in_2(_4_bit_register_3_output), .in_3(_4_bit_register_4_output), .out(output_1));
  Multiplexer #(.Selector_Bits(2), .Bits(4)) multiplexer_2 (
    .sel(read_2), .in_0(_4_bit_register_1_output), .in_1(_4_bit_register_2_output),
    .in_2(_4_bit_register_3_output), .in_3(_4_bit_register_4_output), .out(output_2));
endmodule
